// Logisim project Arquitetura de Computadores Avaliação 1.circ as structural Verilog: 1 circuit, main circuit main
module main (
  input  in_1,
  input  in_2,
  input  in_3,
  input  in_4,
  input  in_5,
  input  in_6
);

  wire clock_1_out, main_1__2_0, main_1__2_1, main_1__2_2, main_2_saida1, main_2_saida2, main_2_saida3,
       main_3_a, main_3_b, main_3_c, main_3_d, main_3_e, main_3_f, main_3_g;

  somador_3bits_main main_1 (
    .a0(in_3), .a1(in_2), .a2(in_1), .b0(in_6), .b1(in_5), .b2(in_4), ._2_0(main_1__2_0), ._2_1(main_1__2_1),
    ._2_2(main_1__2_2));
  Clock clock_1 (.out(clock_1_out));
  registrador_3bits_main main_2 (
    .Controle(clock_1_out), .Entrada1(main_1__2_0), .Entrada2(main_1__2_1), .Entrada3(main_1__2_2),
    .Saida1(main_2_saida1), .Saida2(main_2_saida2), .Saida3(main_2_saida3));
  decodificador_main main_3 (
    .bit3(main_2_saida3), .bit2(main_2_saida2), .bit1(main_2_saida1), .A(main_3_a), .B(main_3_b),
    .C(main_3_c), .E(main_3_e), .F(main_3_f), .G(main_3_g), .D(main_3_d));
  _7_Segment_Display u_7_segment_display_1 (
    .g(main_3_a), .f(main_3_b), .a(main_3_c), .b(main_3_d), .e(main_3_e), .d(main_3_f), .c(main_3_g));  // open: dp
endmodule
