// Logisim project completo_somador.circ as structural Verilog: 1 circuit, main circuit main
module main (
  input  A,
  input  B,
  input  Carry_entrada,
  output Saida,
  output Saida_Carry
);

  wire and_1_out, and_2_out, and_3_out;

  ExactlyOne xor_1 (.out(Saida), .in0(A), .in2(Carry_entrada), .in4(B));
  and and_1 (and_1_out, A, B);
  and and_2 (and_2_out, A, Carry_entrada);
  and and_3 (and_3_out, B, Carry_entrada);
  ExactlyOne xor_2 (.out(Saida_Carry), .in0(and_1_out), .in2(and_2_out), .in4(and_3_out));
endmodule
