// Logisim project decode_outA.circ as structural Verilog: 1 circuit, main circuit main
module main (
  input  in_1,
  input  in_2,
  input  in_3,
  output A
);

  wire and_1_out, not_1_out, xor_1_out;

  not not_1 (not_1_out, in_3);
  xor xor_1 (xor_1_out, in_1, in_2);
  and and_1 (and_1_out, in_2, not_1_out);
  or or_1 (A, xor_1_out, and_1_out);
endmodule
