// Logisim project decode_outB.circ as structural Verilog: 1 circuit, main circuit main
module main (
  input  in_1,
  input  in_2,
  input  in_3,
  output B
);

  wire and_1_out, and_2_out, not_1_out, not_2_out, not_3_out, or_1_out;

  not not_1 (not_1_out, in_1);
  not not_2 (not_2_out, in_2);
  not not_3 (not_3_out, in_3);
  or or_1 (or_1_out, in_1, not_3_out);
  and and_1 (and_1_out, in_1, not_3_out);
  and and_2 (and_2_out, or_1_out, not_2_out);
  or or_2 (B, and_2_out, and_1_out);
endmodule
