// Logisim project decode_outC.circ as structural Verilog: 1 circuit, main circuit main
module main (
  input  bit3,
  input  bit2,
  input  bit1,
  output Saida_C
);

  wire xnor_1_out;

  xnor xnor_1 (xnor_1_out, bit3, bit1);
  or or_1 (Saida_C, xnor_1_out, bit2);
endmodule
