// Logisim project decode_outD.circ as structural Verilog: 1 circuit, main circuit main
module main (
  input  bit3,
  input  bit2,
  input  bit1,
  output D
);

  wire not_1_out, xnor_1_out;

  not not_1 (not_1_out, bit3);
  xnor xnor_1 (xnor_1_out, bit1, bit2);
  or or_1 (D, not_1_out, xnor_1_out);
endmodule
