// Logisim project decode_outE.circ as structural Verilog: 1 circuit, main circuit main
module main (
  input  in_1,
  input  in_2,
  input  in_3,
  output E
);

  wire not_1_out, not_2_out, or_1_out;

  not not_1 (not_1_out, in_1);
  not not_2 (not_2_out, in_3);
  or or_1 (or_1_out, in_2, not_1_out);
  and and_1 (E, or_1_out, not_2_out);
endmodule
