// Logisim project decode_outG.circ as structural Verilog: 1 circuit, main circuit main
module main (
  input  in_1,
  input  in_2,
  input  in_3,
  output G
);

  wire not_1_out;

  not not_1 (not_1_out, in_2);
  or or_1 (G, in_3, not_1_out, in_1);
endmodule
