// Logisim project decodificador.circ as structural Verilog: 1 circuit, main circuit main
module main (
  input  bit3,
  input  bit2,
  input  bit1,
  output A,
  output B,
  output C,
  output D,
  output F,
  output E,
  output G
);

  decode_outA_main main_1 (.A(A), .in_1(bit3), .in_2(bit2), .in_3(bit1));
  decode_outB_main main_2 (.B(B), .in_1(bit3), .in_2(bit2), .in_3(bit1));
  decode_outC_main main_3 (.Saida_C(C), .bit3(bit3), .bit2(bit2), .bit1(bit1));
  decode_outD_main main_4 (.D(D), .bit3(bit3), .bit2(bit2), .bit1(bit1));
  decode_outE_main main_5 (.E(E), .in_1(bit3), .in_2(bit2), .in_3(bit1));
  decode_outF_main main_6 (.F(F), .in_1(bit3), .in_2(bit2), .in_3(bit1));
  decode_outG_main main_7 (.G(G), .in_1(bit3), .in_2(bit2), .in_3(bit1));
endmodule
