// Logisim project meio_somador.circ as structural Verilog: 1 circuit, main circuit main
module main (
  input  Entrada_1,
  input  Entrada_2,
  output Saida,
  output Carry_Saida
);

  xor xor_1 (Saida, Entrada_1, Entrada_2);
  and and_1 (Carry_Saida, Entrada_1, Entrada_2);
endmodule
