// Logisim project registrador_1bit.circ as structural Verilog: 1 circuit, main circuit main
module main (
  input  Entrada,
  input  Controle,
  output Saida
);

  wire and_1_out, and_2_out, nor_1_out, not_1_out;

  not not_1 (not_1_out, Entrada);
  and and_1 (and_1_out, Entrada, Controle);
  and and_2 (and_2_out, Controle, not_1_out);
  nor nor_1 (nor_1_out, and_1_out, Saida);
  nor nor_2 (Saida, nor_1_out, and_2_out);
endmodule
