// Logisim project registrador_3bits.circ as structural Verilog: 1 circuit, main circuit main
module main (
  input  Controle,
  input  Entrada1,
  input  Entrada2,
  input  Entrada3,
  output Bit1,
  output Bit3,
  output Bit_2
);

  registrador_1bit_main main_1 (.Entrada(Entrada1), .Controle(Controle), .Saida(Bit1));
  registrador_1bit_main main_2 (.Entrada(Entrada2), .Controle(Controle), .Saida(Bit_2));
  registrador_1bit_main main_3 (.Entrada(Entrada3), .Controle(Controle), .Saida(Bit3));
endmodule
