// Logisim project segmento_a.circ as structural Verilog: 1 circuit, main circuit main
module main (
  input  Bit1,
  input  Bit2,
  input  Bit3,
  output out_4
);

  wire and_1_out, and_2_out, and_3_out, or_1_out;

  and and_1 (and_1_out, ~Bit1, Bit2);  // AND_Gate
  and and_2 (and_2_out, Bit1, ~Bit2);  // AND_Gate
  and and_3 (and_3_out, Bit2, ~Bit3);  // AND_Gate
  or or_1 (or_1_out, and_1_out, and_2_out);
  or or_2 (out_4, or_1_out, and_3_out);
endmodule
