// Logisim project somador_3bits.circ as structural Verilog: 1 circuit, main circuit main
module main (
  input  a0,
  input  a1,
  input  a2,
  input  b0,
  input  b1,
  input  b2,
  output _2_0,
  output _2_1,
  output _2_2,
  output Carry_saida
);

  wire main_1_carry_saida, main_2_saida_carry;

  meio_somador_main main_1 (.Entrada_1(a0), .Entrada_2(b0), .Saida(_2_0), .Carry_Saida(main_1_carry_saida));
  completo_somador_main main_2 (
    .A(a1), .B(b1), .Carry_entrada(main_1_carry_saida), .Saida(_2_1), .Saida_Carry(main_2_saida_carry));
  completo_somador_main main_3 (
    .A(a2), .B(b2), .Carry_entrada(main_2_saida_carry), .Saida(_2_2), .Saida_Carry(Carry_saida));
endmodule
