// Logisim project somador_4bits.circ as structural Verilog: 1 circuit, main circuit main
module main (
  input  a0,
  input  a1,
  input  a2,
  input  a3,
  input  b0,
  input  b1,
  input  b2,
  input  b3,
  output Bit_1,
  output Bit_2,
  output Bit_3,
  output Bit_4,
  output Carry_saida
);

  wire main_1_carry_saida, main_2_saida_carry, main_3_saida_carry;

  meio_somador_main main_1 (.Entrada_1(a0), .Entrada_2(b0), .Saida(Bit_1), .Carry_Saida(main_1_carry_saida));
  completo_somador_main main_2 (
    .A(a1), .B(b1), .Carry_entrada(main_1_carry_saida), .Saida(Bit_2), .Saida_Carry(main_2_saida_carry));
  completo_somador_main main_3 (
    .A(a2), .B(b2), .Carry_entrada(main_2_saida_carry), .Saida(Bit_3), .Saida_Carry(main_3_saida_carry));
  completo_somador_main main_4 (
    .A(a3), .B(b3), .Carry_entrada(main_3_saida_carry), .Saida(Bit_4), .Saida_Carry(Carry_saida));
endmodule
